# Fritzing sketch Connections (saved by Fritzing 0.9.3b)

parts:
  Part1 = Arduino Uno (Rev3) - ICSP
  M2 = Stepper Motor - Bipolar
  R1 = Resistor [tolerance=±5% resistance=220 package=THT]
  R2 = Resistor [tolerance=±5% resistance=220 package=THT]
  R3 = Resistor [tolerance=±5% resistance=220 package=THT]
  R4 = Resistor [tolerance=±5% resistance=220 package=THT]
  R5 = Resistor [tolerance=±5% resistance=220 package=THT]  # not connected
  R6 = Resistor [tolerance=±5% resistance=220 package=THT]  # not connected
  R7 = Resistor [tolerance=±5% resistance=220 package=THT]
  R8 = Resistor [tolerance=±5% resistance=220 package=THT]
  R9 = Resistor [tolerance=±5% resistance=220 package=THT]
  R10 = Resistor [tolerance=±5% resistance=220 package=THT]
  R11 = Resistor [tolerance=±5% resistance=220 package=THT]
  R12 = Resistor [tolerance=±5% resistance=220 package=THT]
  R13 = Resistor [tolerance=±5% resistance=220 package=THT]
  R14 = Resistor [tolerance=±5% resistance=220 package=THT]
  R15 = Resistor [tolerance=±5% resistance=220 package="2512 [SMD]"]
  R16 = Resistor [tolerance=±5% resistance=220 package="2512 [SMD]"]
  R17 = Resistor [tolerance=±5% resistance=220 package="2512 [SMD]"]
  R18 = Resistor [tolerance=±5% resistance=220 package="2512 [SMD]"]
  Raspberry_Pi_1 = Raspberry Pi 3 [part_number=RPI-3-V1.2]
  S1 = Momentary Switch [package=ksa_sealed_tac_switch]

nets:
  N1: Part1.D4, R16.Pin_0
  N2: Part1.D5_PWM, R17.Pin_0
  N3: Part1.D6_PWM, R4.Pin_1
  N4: Part1.D7, R2.Pin_1
  N5: Part1.5V, R1.Pin_1, R3.Pin_1, R18.Pin_0
  N6: Part1.GND, R7.Pin_1, R14.Pin_0, R15.Pin_0
  N7: M2.A, R9.Pin_1
  N8: M2.C, R10.Pin_1
  N9: M2.B, R11.Pin_1
  N10: M2.D, R12.Pin_1
  N11: R8.Pin_1, R13.Pin_0
  N12: Raspberry_Pi_1.3v3, S1.1
  N13: Raspberry_Pi_1.GPIO27, S1.4
  N14: Raspberry_Pi_1.GND, S1.3

notes:
  DM 556
  PUL +
  PUL -
  DIR +
  DIR -
  ENA +
  ENA -
  GND
  V+
  A+
  A-
  B+
  B-
  power supply
  +
  -
  HX711
  GND
  DT
  SCK
  VCC
